# Fritzing sketch schematic (saved by Fritzing 0.9.3b)
breadboards: 1

parts:
  M1 = DC Motor
  S1 = H-Bridge with L298N
  Part1 = Arduino Uno (Rev3)  # not connected
  S2 = Pushbutton [package="[SMD]"]

nets:
  N1: M1.pin_1, S1.M2-02
  N2: M1.pin_2, S1.M2-01
  N3: S2.Pin_1, S2.Pin_2
  N4: S2.Pin_3, S2.Pin_4

custom parts:
  H-Bridge with L298N: h-bridge
